# Fritzing sketch esp (saved by Fritzing 0.9.3b)
circuit board: 8.46667cm x 5.64444cm
breadboards: 1

parts:
  RGB_LED = RGB LED (com. anode, rbg) [package="5 mm [THT]"]
  W2 = ESP-WROOM2-02 full breakout [package="DIP (Dual Inline) [THT]"]
  R1 = Resistor [tolerance=±5% resistance=270 package="2010 [SMD]"]
  R2 = Resistor [tolerance=±5% resistance=270 package="2010 [SMD]"]
  R3 = Resistor [tolerance=±5% resistance=270 package="2010 [SMD]"]

nets:
  N1: RGB_LED.red_cathode, R2.Pin_1
  N2: RGB_LED.common_anode, W2.GND
  N3: RGB_LED.blue_cathode, R1.Pin_1
  N4: RGB_LED.green_cathode, R3.Pin_1
  N5: W2.IO14, R2.Pin_0
  N6: W2.IO12, R1.Pin_0
  N7: W2.IO15, R3.Pin_0
