# Fritzing sketch nodemcu (saved by Fritzing 0.9.3b)
breadboards: 1

parts:
  RGB_LED = RGB LED (com. anode, rbg) [package="5 mm [THT]"]
  R3 = Resistor [tolerance=±5% resistance=270 package="2010 [SMD]"]
  U1 = NodeMCU V1.0
  R2 = Resistor [tolerance=±5% resistance=270 package="2010 [SMD]"]
  R4 = Resistor [tolerance=±5% resistance=270 package="2010 [SMD]"]

nets:
  N1: RGB_LED.red_cathode, R4.Pin_0
  N2: RGB_LED.common_anode, U1.GND
  N3: RGB_LED.blue_cathode, R2.Pin_0
  N4: RGB_LED.green_cathode, R3.Pin_0
  N5: R3.Pin_1, U1.D3
  N6: U1.D1, R4.Pin_1
  N7: U1.D2, R2.Pin_1

custom parts:
  NodeMCU V1.0: ESP8266 based NodeMCU
